# Fritzing sketch buzzer (saved by Fritzing 0.9.6b)
breadboards: 1

parts:
  J2 = Piezo Speaker
  R2 = Resistor [tolerance=±5% power=0.25 resistance=220 package=THT]
  Mod2 = Raspberry Pi 4B

nets:
  N1: J2.pin1, Mod2.GND
  N2: J2.pin2, R2.Pin_0
  N3: R2.Pin_1, Mod2.GPIO18
