# Fritzing sketch servo (saved by Fritzing 0.9.6b)
breadboards: 1

parts:
  Mod1 = Raspberry Pi 4B
  Part2 = Logic Level Converter
  J1 = Basic Servo

nets:
  N1: Mod1.3V3, Part2.LV
  N2: Mod1.5V, Part2.HV
  GND: Mod1.GND, Part2.GND, J1.gnd
  N3: Mod1.GPIO13, Part2.TX2_LV
  N4: Part2.TX2_HV, J1.pulse
