# Fritzing sketch schemat_lidar (saved by Fritzing 0.9.3b)
breadboards: 1

parts:
  Mod1 = Raspberry Pi 4B
  Part4 = Logic Level Converter
  J2 = Basic Servo
  R4 = Resistor [tolerance=±5% resistance=10k package="0402 [SMD]"]
  R5 = Resistor [tolerance=±5% resistance=4.7k package="0402 [SMD]"]
  R6 = Resistor [tolerance=±5% resistance=4.7k package="0402 [SMD]"]
  Part5 = Adafruit VL530X Time of Flight Distance Sensor [part_number="Adafruit #3317"]

nets:
  3V3: Mod1.3V3, Part4.LV, R4.Pin_1, R5.Pin_1, R6.Pin_1, Part5.VCC
  N1: Mod1.GPIO2, R5.Pin_0, Part5.SDA
  N2: Mod1.GPIO3, R6.Pin_0, Part5.SCL
  GND: Mod1.GND, Part4.GND, J2.gnd, Part5.GND
  N3: Mod1.GPIO25, Part4.TX2_LV
  N4: Part4.HV, J2.vcc
  N5: Part4.TX2_HV, J2.pulse
  N6: R4.Pin_0, Part5.XSHUT

custom parts:
  Adafruit VL530X Time of Flight Distance Sensor: The VL53L0X is a Time of Flight distance sensor like no other you've used! The sensor contains a very tiny invisible laser source, and a matching sensor. The VL53L0X can detect the "time of flight", or how long the light has taken to bounce back to the sensor. Since it uses a very narrow light source, it is good for determining distance of only the surface directly in front of it. Unlike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
